# Fritzing sketch Esquema-SuperWaterSaver (saved by Fritzing 0.9.3b)
breadboards: 1

parts:
  U1 = LCD-16X2 [package=lcd-16x2_noholes]
  R1 = Rotary Potentiometer (Large) [maximum_resistance=100kΩ package=THT]
  Componente1 = Arduino Uno (Rev3) - ICSP
  YF-S201_Flow_Meter1 = YF-S201 Water Flow Meter

nets:
  VSS: U1.VSS, U1.R_W, U1.K, R1.leg2, Componente1.GND, YF-S201_Flow_Meter1.SIG
  VDD: U1.VDD, U1.A, R1.leg1, Componente1.5V, YF-S201_Flow_Meter1.VCC
  N1: U1.VO, R1.wiper
  N2: U1.RS, Componente1.D7
  N3: U1.E, Componente1.D8
  N4: U1.DB4, Componente1.D9_PWM
  N5: U1.DB5, Componente1.D10_PWM/SS
  N6: U1.DB6, Componente1.D11_PWM/MOSI
  N7: U1.DB7, Componente1.ICSP_MISO, Componente1.D12/MISO
  N8: Componente1.D2, YF-S201_Flow_Meter1.GND

notes:
  Caudalímetro
  D2
  Pantalla LCD 16x2
  Potenciómetro
  Arduino Uno

custom parts:
  YF-S201 Water Flow Meter: The YF-S201 Flow Meter. The input voltage is 5V to 24V (DC).
